// Logisim project ps2_interface_sim.circ as structural Verilog: 1 circuit, main circuit main
module main (
  input  CLK,
  input  DAT
);

  wire button_1_out, n74161_1_pin3, n74161_1_pin7, n74161_1_pin9, n74161_1_pin10, n74161_1_pin11,
       n74161_1_pin13, n74161_1_pin14, n74161_1_pin15, n74164_1_pin3, n74164_1_pin4, n74164_1_pin5,
       n74164_1_pin6, n74164_1_pin10, n74164_1_pin11, n74164_1_pin12, n74164_1_pin13, n74164_2_pin3,
       n74164_2_pin4, n74164_2_pin5, nand_1_out, nand_2_out, nand_3_out;

  Button #(.press("passive")) button_1 (.out(button_1_out));
  _74164 u_74164_1 (
    .pin1(DAT), .pin2(DAT), .pin3(n74164_1_pin3), .pin4(n74164_1_pin4), .pin5(n74164_1_pin5),
    .pin6(n74164_1_pin6), .pin13(n74164_1_pin13), .pin12(n74164_1_pin12), .pin11(n74164_1_pin11),
    .pin10(n74164_1_pin10), .pin9(button_1_out), .pin8(CLK));
  _74164 u_74164_2 (
    .pin1(n74164_1_pin13), .pin2(n74164_1_pin13), .pin3(n74164_2_pin3), .pin4(n74164_2_pin4),
    .pin5(n74164_2_pin5), .pin9(button_1_out), .pin8(CLK));  // open: pin6, pin13, pin12, pin11, pin10
  _74161 u_74161_1 (
    .pin1(button_1_out), .pin2(CLK), .pin3(n74161_1_pin3), .pin4(n74161_1_pin3), .pin5(n74161_1_pin3),
    .pin6(n74161_1_pin3), .pin7(n74161_1_pin7), .pin15(n74161_1_pin15), .pin14(n74161_1_pin14),
    .pin13(n74161_1_pin13), .pin11(n74161_1_pin11), .pin10(n74161_1_pin10), .pin9(n74161_1_pin9));  // open: pin12
  // NoConnect on n74161_1_pin15
  nand nand_1 (nand_1_out, n74161_1_pin14, n74161_1_pin13);
  nand nand_2 (nand_2_out, nand_1_out, nand_1_out);
  nand nand_3 (nand_3_out, nand_2_out, n74161_1_pin11);
  // also tied to GND on the sheet: n74161_1_pin3
  // also tied to VCC on the sheet: {n74161_1_pin7, n74161_1_pin10, n74161_1_pin9}
endmodule
